# Fritzing sketch Wiring_ESP32NodeMCU_38pin_NRF24 (saved by Fritzing 0.9.10b)

parts:
  U1 = ESP32-38PinWide [part_number=ESP32-38PinWide]
  NRF24 = NRF24L01+ Breakout Board
  Optional_Display = OLED 0.96" 128x64 I2C SSD1306
  LED0 = LED - 3mm [color="Red (633nm)" current=0.030 package="3 mm [THT]"]
  LED1 = LED - 3mm [color="Red (633nm)" current=0.030 package="3 mm [THT]"]
  R1 = Resistor [tolerance=±5% resistance=68 package="0402 [SMD]"]
  R2 = Resistor [tolerance=±5% resistance=68 package="0402 [SMD]"]
  C2 = Electrolytic Capacitor [capacitance=1mF voltage=16V package="100 mil [THT, electrolytic]"]

nets:
  VCC: U1.3.3, NRF24.VCC, Optional_Display.VCC, C2.+
  N1: U1.GPIO25, R1.Pin_0
  N2: U1.GPIO26, R2.Pin_0
  GND: U1.GND, NRF24.GND, Optional_Display.GND, LED0.cathode, LED1.cathode, C2.-
  N3: U1.GPIO4, NRF24.CE
  N4: U1.GPIO16, NRF24.IRQ
  N5: U1.GPIO5, NRF24.CS
  N6: U1.GPIO18, NRF24.SCK
  N7: U1.GPIO19, NRF24.MISO
  N8: U1.GPIO21, Optional_Display.SCA
  N9: U1.GPIO22, Optional_Display.SCL
  N10: U1.GPIO23, NRF24.MOSI
  N11: LED0.anode, R1.Pin_1
  N12: LED1.anode, R2.Pin_1

notes:
  Optional LEDs
  Optional Display
  Connect any
  supported I²C display
  NRF24L01+
  Place the capacitor as close
  to the nRF24 board as possible.

custom parts:
  ESP32-38PinWide: Generic 38-Pin ESP32 with wide format (only access to one side of pins on a breadboard) based on Stephen Lilley's HiLetgo ESP-WROOM-32 ESP32 ESP-32S Development Board.
